// Logisim project IT012_Lab01_25520668.circ as structural Verilog: 5 circuits, main circuit TN1
module TN1 (
  input  C,
  input  A,
  input  B,
  output NAND3,
  output XOR3,
  output out_6,
  output AND,
  output OR,
  output NAND,
  output NOR,
  output XOR,
  output XNOR,
  output CHAIN
);

  wire nand_3_out;

  nand nand_1 (NAND3, B, A, C);
  xor xor_1 (XOR3, B, A, C);
  not not_1 (out_6, A);
  and and_1 (AND, A, B);
  or or_1 (OR, A, B);
  nand nand_2 (NAND, A, B);
  nor nor_1 (NOR, A, B);
  xor xor_2 (XOR, A, B);
  xnor xnor_1 (XNOR, A, B);
  nand nand_3 (nand_3_out, A, B);
  nand Y (CHAIN, nand_3_out, C);
endmodule

module TN2 (
  input  x,
  input  y,
  input  z,
  output EQ1,
  output EQ2,
  output EQ3,
  output EQ4,
  output EQ5
);

  wire and_1_out, and_2_out, and_3_out, not_1_out, not_2_out, not_3_out, or_1_out, or_2_out, VP1_out,
       VP3_out, VP5_out, VT1_out, VT2_out, VT3_out, VT4_out;

  not not_1 (not_1_out, x);
  not not_2 (not_2_out, x);
  not not_3 (not_3_out, y);
  and and_1 (and_1_out, not_1_out, y);
  and VP1 (VP1_out, not_2_out, not_3_out);
  or or_1 (or_1_out, x, y);
  and and_2 (and_2_out, x, y);
  and and_3 (and_3_out, y, z);
  or or_2 (or_2_out, x, z);
  or VT4 (VT4_out, and_1_out, x);
  or VP5 (VP5_out, x, y);
  not VT1 (VT1_out, or_1_out);
  not VT2 (VT2_out, and_2_out);
  or VT3 (VT3_out, and_3_out, x);
  and VP3 (VP3_out, or_1_out, or_2_out);
  xnor xnor_1 (EQ1, VP1_out, VT1_out);
  xnor xnor_2 (EQ4, VT4_out, x);
  xnor xnor_3 (EQ5, VP5_out, VT4_out);
  xnor xnor_4 (EQ2, VP1_out, VT2_out);
  xnor xnor_5 (EQ3, VT3_out, VP3_out);
endmodule

module TN3 (
  input  A,
  input  B,
  input  C,
  input  D,
  output F
);

  wire m2_out, m3_out, m5_out, m7_out, m11_out, m13_out, not_1_out, not_2_out, not_3_out, not_4_out;

  not not_1 (not_1_out, A);
  not not_2 (not_2_out, B);
  not not_3 (not_3_out, C);
  not not_4 (not_4_out, D);
  and m2 (m2_out, not_1_out, not_2_out, C, not_4_out);
  and m3 (m3_out, not_2_out, not_1_out, C, D);
  and m5 (m5_out, not_1_out, B, not_3_out, D);
  and m7 (m7_out, not_1_out, B, C, D);
  and m11 (m11_out, A, not_2_out, C, D);
  and m13 (m13_out, A, B, not_3_out, D);
  or or_1 (F, m2_out, m3_out, m5_out, m7_out, m11_out, m13_out);
endmodule

module TN4 (
  input  A,
  input  B,
  input  C,
  input  D,
  output F_can,
  output F_sop,
  output F_pos
);

  wire _1_2_out, _1_out, _2_2_out, _2_out, _3_2_out, _3_out, _4_2_out, _4_out, _5_out, m2_out, m3_out,
       m5_out, m7_out, m11_out, m13_out, not_1_out, not_2_out, not_3_out, not_4_out, not_5_out, not_6_out,
       not_7_out;

  not not_1 (not_1_out, A);
  not not_2 (not_2_out, A);
  not not_3 (not_3_out, B);
  not not_4 (not_4_out, B);
  not not_5 (not_5_out, C);
  not not_6 (not_6_out, C);
  or _1 (_1_out, C, D);
  or _2 (_2_out, B, C);
  or _3 (_3_out, not_2_out, D);
  or _4 (_4_out, not_2_out, not_3_out, not_6_out);
  or _5 (_5_out, D, not_3_out);
  not not_7 (not_7_out, D);
  and _1_2 (_1_2_out, not_1_out, not_4_out, C);
  and _2_2 (_2_2_out, not_4_out, C, D);
  and _3_2 (_3_2_out, not_1_out, B, D);
  and _4_2 (_4_2_out, B, not_5_out, D);
  and m2 (m2_out, not_2_out, not_3_out, C, not_7_out);
  and m3 (m3_out, not_3_out, not_2_out, C, D);
  and m5 (m5_out, not_2_out, B, not_6_out, D);
  and m7 (m7_out, not_2_out, B, C, D);
  and m11 (m11_out, A, not_3_out, C, D);
  and m13 (m13_out, A, B, not_6_out, D);
  or or_1 (F_sop, _1_2_out, _2_2_out, _3_2_out, _4_2_out);
  and and_1 (F_pos, _1_out, _2_out, _3_out, _4_out, _5_out);
  or or_2 (F_can, m2_out, m3_out, m5_out, m7_out, m11_out, m13_out);
endmodule

module TN5 (
  input  A,
  input  B,
  input  C,
  output F
);

  wire xor_1_out;

  xor xor_1 (xor_1_out, A, B);
  xor xor_2 (F, xor_1_out, C);
endmodule
